# Fritzing sketch Test Rig (saved by Fritzing 0.9.3b)
breadboards: 1

parts:
  Part1 = Arduino Uno (Rev3)
  R1 = Resistor [tolerance=±5% resistance=5.1k package="0805 [SMD]"]
  R2 = Resistor [tolerance=±5% resistance=5.1k package="0805 [SMD]"]
  R3 = Resistor [tolerance=±5% resistance=5.1k package="0805 [SMD]"]
  R4 = Resistor [tolerance=±5% resistance=5.1k package="0805 [SMD]"]
  T1 = Temperature Sensor (Thermistor) [thermistor_type=NTC package=THT]
  T2 = Temperature Sensor (Thermistor) [thermistor_type=NTC package=THT]
  T3 = Temperature Sensor (Thermistor) [thermistor_type=NTC package=THT]
  T4 = Temperature Sensor (Thermistor) [thermistor_type=NTC package=THT]
  U1 = mystery part, 3 pins [chip_label="Current Sensor" part_number=ACS759]
  Linear_Actuator_Feedback = Rotary Potentiometer (Small) [maximum_resistance=10kΩ package=THT]
  R5 = Resistor [tolerance=±5% resistance=220 package=THT]
  R6 = Resistor [tolerance=±5% resistance=10k package=THT]
  Photoreflective_Sensor = QRD1114 [part_number=QRD1113 package=qrd1114]
  U3 = RELAY [package=relay-jzc]
  U4 = RELAY [package=relay-jzc]
  Linear_Actuator = DC Motor
  LED_Power_Supply = DC Power [voltage=12V]
  IC1 = IC, DIP package, 14 pins [chip_label="Shift Register" part_number=74LS164]
  IC2 = IC, DIP package, 20 pins [chip_label="Quad DAC" part_number=TLC7226]
  U2 = mystery part, 2 pins [chip_label="Motor Controller"]

nets:
  N1: Part1.A0, U1.pin3
  N2: Part1.A1, R1.Pin_1, T1.pin_0
  N3: Part1.A2, R2.Pin_1, T2.pin_0
  N4: Part1.A3, R3.Pin_1, T3.pin_0
  N5: Part1.A4/SDA, R4.Pin_1, T4.pin_0
  N6: Part1.D8, IC1.pin1, IC1.pin2
  N7: Part1.D9_PWM, IC1.pin8
  N8: Part1.D10_PWM/SS, IC2.pin15
  N9: Part1.D11_PWM/MOSI, IC2.pin16
  N10: Part1.D12/MISO, IC2.pin17
  N11: Part1.GND, Linear_Actuator_Feedback.leg1, U3.COIL2
  N12: Part1.A5/SCL, Linear_Actuator_Feedback.wiper
  N13: Part1.D2, R6.Pin_1, Photoreflective_Sensor.E
  N14: Part1.D6_PWM, U4.COIL1
  N15: Part1.D7, U3.COIL1
  N16: Part1.3V3, U1.pin1
  N17: Part1.5V, T1.pin_1, T2.pin_1, T3.pin_1, T4.pin_1, Linear_Actuator_Feedback.leg2, R5.Pin_0, R6.Pin_0, IC1.pin14
  N18: R1.Pin_0, R2.Pin_0, R3.Pin_0, R4.Pin_0
  GND: U1.pin2, Photoreflective_Sensor.C, Photoreflective_Sensor.K, IC1.pin7, IC2.pin3, IC2.pin5, IC2.pin6, U2.pin2
  N19: R5.Pin_1, Photoreflective_Sensor.A
  N20: U3.NC, U4.NC, LED_Power_Supply.V+
  N21: U3.NO, U4.COIL2, U4.NO, LED_Power_Supply.V-
  N22: U3.MAIN, Linear_Actuator.pin_2
  N23: U4.MAIN, Linear_Actuator.pin_1
  N24: IC1.pin3, IC2.pin14
  N25: IC1.pin4, IC2.pin13
  N26: IC1.pin5, IC2.pin12
  N27: IC1.pin6, IC2.pin11
  N28: IC1.pin9, IC2.pin4, IC2.pin18
  N29: IC1.pin10, IC2.pin10
  N30: IC1.pin11, IC2.pin9
  N31: IC1.pin12, IC2.pin8
  N32: IC1.pin13, IC2.pin7
  N33: IC2.pin2, U2.pin1
